# Fritzing sketch SmartHome (saved by Fritzing 0.9.1b)
breadboards: 1

parts:
  RHT1 = Humidity and Temperature Sensor RHT03
  U1 = PIR Sensor HC-SR501
  Часть2 = BH1750FVI Breakout Board [part_number=BH1750FVI]
  Часть3 = Arduino Uno (Rev3)
  Espessif_Serial_Wifi_Modul_1 = ESP8266 ESP01 [part_number=ESP8266 package=THT]
  Power_plug1 = Power plug
  Часть4 = FC-28 Soil Hygrometer Module

nets:
  VCC: RHT1.Vcc, U1.VCC, Часть2.VCC, Часть3.5V, Часть4.VCC
  N1: RHT1.Data-signal, Часть3.A0
  GND: RHT1.GND_1, U1.GND, Часть2.GND, Часть3.GND, Espessif_Serial_Wifi_Modul_1.GND, Power_plug1.GND, Часть4.GND
  N2: U1.OUT, Часть3.D12/MISO
  N3: Часть3.D0/RX, Espessif_Serial_Wifi_Modul_1.TXD
  N4: Часть3.D1/TX, Espessif_Serial_Wifi_Modul_1.RXD
  VCC_2: Espessif_Serial_Wifi_Modul_1.VCC, Espessif_Serial_Wifi_Modul_1.CH_PD, Power_plug1.VCC

notes:
  DC 3.3 V

custom parts:
  PIR Sensor HC-SR501: Passive Infra-Red (PIR) sensor HC-SR501
  BH1750FVI Breakout Board: The ROHM Semiconductor BH1750FVI is a digital ambient light sensor for the I2C bus interface. The BH750FVI is able to detect a wide range of light intensities (1-65535 lux). The spectral range is similar to that of the human eye.
  ESP8266 ESP01: Generic WiFi Module based on the ESP8266 with onboard PCB antenna and UART communications
  FC-28 Soil Hygrometer Module: The FC-28 is a soil hygrometer module that uses the Texas Instruments LM393 comparator chip to provide an analog measurement of soil humidity. The digital output is high when soil moisture is over a certain threshold, as determined by adjusting the potentiometer.
